// Digital circuit ALU-completa.dig as structural Verilog
module ALU_completa (
  input  [2:0] Seletor,
  input  [7:0] in_2,
  input  [7:0] in_3
);

  wire _0, decoder_1_out_0, decoder_1_out_1, decoder_1_out_2, decoder_1_out_3, decoder_1_out_4,
       decoder_1_out_5, decoder_1_out_6, somador_8bits_1_p3;
  wire [7:0] circuito_subtracao_1_s, divisor_8bits_completo_1_q, divisor_8bits_completo_1_r, driver_1_out,
       driver_8_out, multiplicador_final_8bits_1_ac, multiplicador_final_8bits_1_mq, nand_1_nand,
       shift_left_1_a_2, somador_8bits_1_p4, xor_1_xor;

  Decoder #(.Selector_Bits(3)) decoder_1 (
    .sel(Seletor), .out_0(decoder_1_out_0), .out_1(decoder_1_out_1), .out_2(decoder_1_out_2),
    .out_3(decoder_1_out_3), .out_4(decoder_1_out_4), .out_5(decoder_1_out_5), .out_6(decoder_1_out_6),
    .out_7(_0));
  // somador_8bits somador_8bits_1: pin names not known; wires that end beside it: in_2, in_3, somador_8bits_1_p3, somador_8bits_1_p4
  circuito_subtracao circuito_subtracao_1 (.A(in_2), .N(in_3), .Cout(somador_8bits_1_p3), .S(circuito_subtracao_1_s));
  multiplicador_final_8bits multiplicador_final_8bits_1 (
    .A(in_2), .N(in_3), .AC(multiplicador_final_8bits_1_ac), .MQ(multiplicador_final_8bits_1_mq));
  divisor_8bits_completo divisor_8bits_completo_1 (
    .A(in_2), .N(in_3), .R(divisor_8bits_completo_1_r), .Q(divisor_8bits_completo_1_q));
  shift_left shift_left_1 (.A(in_2), .A_2(shift_left_1_a_2), .Cout(somador_8bits_1_p3));
  NAND nand_1 (.A(in_2), .N(in_3), .NAND(nand_1_nand));
  XOR xor_1 (.A(in_2), .N(in_3), .XOR(xor_1_xor));
  assign driver_1_out = decoder_1_out_0 ? somador_8bits_1_p4 : 8'bz;  // Driver driver_1
  assign driver_1_out = decoder_1_out_1 ? circuito_subtracao_1_s : 8'bz;  // Driver driver_2
  assign driver_1_out = decoder_1_out_2 ? multiplicador_final_8bits_1_ac : 8'bz;  // Driver driver_3
  assign driver_1_out = decoder_1_out_3 ? divisor_8bits_completo_1_q : 8'bz;  // Driver driver_4
  assign driver_1_out = decoder_1_out_4 ? shift_left_1_a_2 : 8'bz;  // Driver driver_5
  assign driver_1_out = decoder_1_out_5 ? nand_1_nand : 8'bz;  // Driver driver_6
  assign driver_1_out = decoder_1_out_6 ? xor_1_xor : 8'bz;  // Driver driver_7
  assign driver_8_out = decoder_1_out_2 ? multiplicador_final_8bits_1_mq : 8'bz;  // Driver driver_8
  assign driver_8_out = decoder_1_out_3 ? divisor_8bits_completo_1_r : 8'bz;  // Driver driver_9
  LED led_1 (.in(somador_8bits_1_p3));
  LED led_2 (.in(driver_8_out[7]));
  LED led_3 (.in(driver_8_out[5]));
  LED led_4 (.in(driver_8_out[6]));
  LED led_5 (.in(driver_8_out[3]));
  LED led_6 (.in(driver_8_out[4]));
  LED led_7 (.in(driver_8_out[2]));
  LED led_8 (.in(driver_8_out[1]));
  LED led_9 (.in(driver_8_out[0]));
  LED led_10 (.in(driver_1_out[7]));
  LED led_11 (.in(driver_1_out[5]));
  LED led_12 (.in(driver_1_out[6]));
  LED led_13 (.in(driver_1_out[3]));
  LED led_14 (.in(driver_1_out[4]));
  LED led_15 (.in(driver_1_out[2]));
  LED led_16 (.in(driver_1_out[1]));
  LED led_17 (.in(driver_1_out[0]));

  // Notes on the sheet:
  //   MQ
  //   Resto
  //   AC
endmodule
