// Digital circuit NAND.dig as structural Verilog
module NAND (
  input  [7:0] A,
  input  [7:0] N,
  output [7:0] NAND
);

  nand nand_1 (NAND[0], A[0], N[0]);
  nand nand_2 (NAND[1], A[1], N[1]);
  nand nand_3 (NAND[2], A[2], N[2]);
  nand nand_4 (NAND[3], A[3], N[3]);
  nand nand_5 (NAND[4], A[4], N[4]);
  nand nand_6 (NAND[5], A[5], N[5]);
  nand nand_7 (NAND[6], A[6], N[6]);
  nand nand_8 (NAND[7], A[7], N[7]);
endmodule
