// Digital circuit XOR.dig as structural Verilog
module XOR (
  input  [7:0] A,
  input  [7:0] N,
  output [7:0] XOR
);

  xor xor_1 (XOR[0], A[0], N[0]);
  xor xor_2 (XOR[1], A[1], N[1]);
  xor xor_3 (XOR[2], A[2], N[2]);
  xor xor_4 (XOR[3], A[3], N[3]);
  xor xor_5 (XOR[4], A[4], N[4]);
  xor xor_6 (XOR[5], A[5], N[5]);
  xor xor_7 (XOR[6], A[6], N[6]);
  xor xor_8 (XOR[7], A[7], N[7]);
endmodule
