// Digital circuit circuito-soma.dig as structural Verilog
module circuito_soma (
  input  A,
  input  B,
  input  C,
  input  D,
  input  E,
  input  F,
  input  G,
  input  H,
  input  I,
  input  J,
  input  K,
  input  L,
  input  M,
  input  N,
  input  O,
  input  P,
  input  Q,
  input  R,
  output S1,
  output S2,
  output S3,
  output S4,
  output S5,
  output S6,
  output S7,
  output S8,
  output S9,
  output Cout
);

  wire and_1_out, and_2_out, and_3_out, and_4_out, and_5_out, and_6_out, and_7_out, and_8_out, and_9_out,
       and_10_out, and_11_out, and_12_out, and_13_out, and_14_out, and_15_out, and_16_out, and_17_out,
       and_18_out, and_19_out, and_20_out, and_21_out, and_22_out, and_23_out, and_24_out, and_25_out,
       and_26_out, and_27_out, or_2_out, or_3_out, or_4_out, or_5_out, or_6_out, or_7_out, or_8_out,
       or_9_out, xor_1_out, xor_3_out, xor_5_out, xor_7_out, xor_9_out, xor_11_out, xor_13_out, xor_15_out,
       xor_17_out;

  xor xor_1 (xor_1_out, Q, R);
  and and_1 (and_1_out, Q, or_2_out);
  and and_2 (and_2_out, R, or_2_out);
  and and_3 (and_3_out, Q, R);
  xor xor_2 (S9, xor_1_out, or_2_out);
  or or_1 (Cout, and_1_out, and_2_out, and_3_out);
  xor xor_3 (xor_3_out, O, P);
  and and_4 (and_4_out, O, or_3_out);
  and and_5 (and_5_out, P, or_3_out);
  and and_6 (and_6_out, O, P);
  xor xor_4 (S8, xor_3_out, or_3_out);
  or or_2 (or_2_out, and_4_out, and_5_out, and_6_out);
  xor xor_5 (xor_5_out, M, N);
  and and_7 (and_7_out, M, or_4_out);
  and and_8 (and_8_out, N, or_4_out);
  and and_9 (and_9_out, M, N);
  xor xor_6 (S7, xor_5_out, or_4_out);
  or or_3 (or_3_out, and_7_out, and_8_out, and_9_out);
  xor xor_7 (xor_7_out, K, L);
  and and_10 (and_10_out, K, or_5_out);
  and and_11 (and_11_out, L, or_5_out);
  and and_12 (and_12_out, K, L);
  xor xor_8 (S6, xor_7_out, or_5_out);
  or or_4 (or_4_out, and_10_out, and_11_out, and_12_out);
  xor xor_9 (xor_9_out, I, J);
  and and_13 (and_13_out, I, or_6_out);
  and and_14 (and_14_out, J, or_6_out);
  and and_15 (and_15_out, I, J);
  xor xor_10 (S5, xor_9_out, or_6_out);
  or or_5 (or_5_out, and_13_out, and_14_out, and_15_out);
  xor xor_11 (xor_11_out, G, H);
  and and_16 (and_16_out, G, or_7_out);
  and and_17 (and_17_out, H, or_7_out);
  and and_18 (and_18_out, G, H);
  xor xor_12 (S4, xor_11_out, or_7_out);
  or or_6 (or_6_out, and_16_out, and_17_out, and_18_out);
  xor xor_13 (xor_13_out, E, F);
  and and_19 (and_19_out, E, or_8_out);
  and and_20 (and_20_out, F, or_8_out);
  and and_21 (and_21_out, E, F);
  xor xor_14 (S3, xor_13_out, or_8_out);
  or or_7 (or_7_out, and_19_out, and_20_out, and_21_out);
  xor xor_15 (xor_15_out, C, D);
  and and_22 (and_22_out, C, or_9_out);
  and and_23 (and_23_out, D, or_9_out);
  and and_24 (and_24_out, C, D);
  xor xor_16 (S2, xor_15_out, or_9_out);
  or or_8 (or_8_out, and_22_out, and_23_out, and_24_out);
  xor xor_17 (xor_17_out, A, B);
  and and_25 (and_25_out, A, 1'b0);
  and and_26 (and_26_out, B, 1'b0);
  and and_27 (and_27_out, A, B);
  xor xor_18 (S1, xor_17_out, 1'b0);
  or or_9 (or_9_out, and_25_out, and_26_out, and_27_out);
endmodule
