// Digital circuit circuito-subtracao.dig as structural Verilog
module circuito_subtracao (
  input  [7:0] A,
  input  [7:0] N,
  output Cout,
  output [7:0] S
);

  wire and_1_out, and_2_out, and_3_out, and_4_out, and_5_out, and_6_out, and_7_out, and_8_out, and_9_out,
       and_10_out, and_11_out, and_12_out, and_13_out, and_14_out, and_15_out, and_16_out, and_17_out,
       and_18_out, and_19_out, and_20_out, and_21_out, and_22_out, and_23_out, and_24_out, not_1_out,
       not_2_out, not_3_out, not_4_out, not_5_out, not_6_out, not_7_out, not_8_out, not_9_out, not_10_out,
       not_11_out, not_12_out, not_13_out, not_14_out, not_15_out, not_16_out, or_3_out, or_4_out, or_5_out,
       or_6_out, or_7_out, or_8_out, xor_1_out, xor_3_out, xor_5_out, xor_7_out, xor_9_out, xor_11_out,
       xor_13_out, xor_15_out;

  xor xor_1 (xor_1_out, A[7], N[7]);
  and and_1 (and_1_out, not_1_out, N[7]);
  not not_1 (not_1_out, A[7]);
  and and_2 (and_2_out, N[7], S[6]);
  and and_3 (and_3_out, not_2_out, S[6]);
  not not_2 (not_2_out, A[7]);
  xor xor_2 (S[7], xor_1_out, S[6]);
  or or_1 (Cout, and_1_out, and_2_out, and_3_out);
  xor xor_3 (xor_3_out, A[6], N[6]);
  not not_3 (not_3_out, A[6]);
  not not_4 (not_4_out, A[6]);
  and and_4 (and_4_out, not_3_out, N[6]);
  and and_5 (and_5_out, N[6], or_3_out);
  and and_6 (and_6_out, not_4_out, or_3_out);
  xor xor_4 (S[6], xor_3_out, or_3_out);
  or or_2 (S[6], and_4_out, and_5_out, and_6_out);
  xor xor_5 (xor_5_out, A[5], N[5]);
  not not_5 (not_5_out, A[5]);
  not not_6 (not_6_out, A[5]);
  and and_7 (and_7_out, not_5_out, N[5]);
  and and_8 (and_8_out, N[5], or_4_out);
  and and_9 (and_9_out, not_6_out, or_4_out);
  xor xor_6 (S[5], xor_5_out, or_4_out);
  or or_3 (or_3_out, and_7_out, and_8_out, and_9_out);
  xor xor_7 (xor_7_out, A[4], N[4]);
  not not_7 (not_7_out, A[4]);
  not not_8 (not_8_out, A[4]);
  and and_10 (and_10_out, not_7_out, N[4]);
  and and_11 (and_11_out, N[4], or_5_out);
  and and_12 (and_12_out, not_8_out, or_5_out);
  xor xor_8 (S[4], xor_7_out, or_5_out);
  or or_4 (or_4_out, and_10_out, and_11_out, and_12_out);
  xor xor_9 (xor_9_out, A[3], N[3]);
  not not_9 (not_9_out, A[3]);
  not not_10 (not_10_out, A[3]);
  and and_13 (and_13_out, not_9_out, N[3]);
  and and_14 (and_14_out, N[3], or_6_out);
  and and_15 (and_15_out, not_10_out, or_6_out);
  xor xor_10 (S[3], xor_9_out, or_6_out);
  or or_5 (or_5_out, and_13_out, and_14_out, and_15_out);
  xor xor_11 (xor_11_out, A[2], N[2]);
  and and_16 (and_16_out, not_11_out, N[2]);
  not not_11 (not_11_out, A[2]);
  and and_17 (and_17_out, N[2], or_7_out);
  and and_18 (and_18_out, not_12_out, or_7_out);
  not not_12 (not_12_out, A[2]);
  xor xor_12 (S[2], xor_11_out, or_7_out);
  or or_6 (or_6_out, and_16_out, and_17_out, and_18_out);
  xor xor_13 (xor_13_out, A[1], N[1]);
  not not_13 (not_13_out, A[1]);
  not not_14 (not_14_out, A[1]);
  and and_19 (and_19_out, not_13_out, N[1]);
  and and_20 (and_20_out, N[1], or_8_out);
  and and_21 (and_21_out, not_14_out, or_8_out);
  xor xor_14 (S[1], xor_13_out, or_8_out);
  or or_7 (or_7_out, and_19_out, and_20_out, and_21_out);
  xor xor_15 (xor_15_out, A[0], N[0]);
  not not_15 (not_15_out, A[0]);
  not not_16 (not_16_out, A[0]);
  and and_22 (and_22_out, not_15_out, N[0]);
  and and_23 (and_23_out, N[0], 1'b0);
  and and_24 (and_24_out, not_16_out, 1'b0);
  xor xor_16 (S[0], xor_15_out, 1'b0);
  or or_8 (or_8_out, and_22_out, and_23_out, and_24_out);
endmodule
