// Digital circuit complemento-de-dois.dig as structural Verilog
module complemento_de_dois (
  input  ctr,
  input  [7:0] A,
  input  [7:0] B,
  output [7:0] S,
  output C
);

  wire full_adder_1_p5, full_adder_2_p5, full_adder_3_p5, full_adder_4_p5, full_adder_5_p5, full_adder_6_p5,
       full_adder_7_p5, full_adder_8_p5, not_1_out, xor_1_out, xor_2_out, xor_3_out, xor_4_out, xor_5_out,
       xor_6_out, xor_7_out, xor_8_out;

  xor xor_1 (xor_1_out, ctr, B[0]);
  xor xor_2 (xor_2_out, ctr, B[1]);
  // full_adder full_adder_1: pin names not known; wires that end beside it: A[0], xor_1_out, ctr, S[0], full_adder_1_p5
  xor xor_3 (xor_3_out, ctr, B[2]);
  // full_adder full_adder_2: pin names not known; wires that end beside it: A[1], xor_2_out, full_adder_1_p5, S[1], full_adder_2_p5
  xor xor_4 (xor_4_out, ctr, B[3]);
  // full_adder full_adder_3: pin names not known; wires that end beside it: A[2], xor_3_out, full_adder_2_p5, S[2], full_adder_3_p5
  xor xor_5 (xor_5_out, ctr, B[4]);
  // full_adder full_adder_4: pin names not known; wires that end beside it: A[3], xor_4_out, full_adder_3_p5, S[3], full_adder_4_p5
  xor xor_6 (xor_6_out, ctr, B[5]);
  // full_adder full_adder_5: pin names not known; wires that end beside it: A[4], xor_5_out, full_adder_4_p5, S[4], full_adder_5_p5
  xor xor_7 (xor_7_out, ctr, B[6]);
  xor xor_8 (xor_8_out, ctr, B[7]);
  // full_adder full_adder_6: pin names not known; wires that end beside it: A[5], xor_6_out, full_adder_5_p5, S[5], full_adder_6_p5
  // full_adder full_adder_7: pin names not known; wires that end beside it: A[6], xor_7_out, full_adder_6_p5, S[6], full_adder_7_p5
  // full_adder full_adder_8: pin names not known; wires that end beside it: A[7], xor_8_out, full_adder_7_p5, S[7], full_adder_8_p5
  not not_1 (not_1_out, full_adder_8_p5);
  and and_1 (C, not_1_out, ctr);
endmodule
