// Digital circuit divisor-8bits-completo.dig as structural Verilog
module divisor_8bits_completo (
  input  [7:0] A,
  input  [7:0] N,
  output [7:0] R,
  output [7:0] Q
);

  wire complemento_de_dois_1_c, complemento_de_dois_2_c, complemento_de_dois_3_c, complemento_de_dois_4_c,
       complemento_de_dois_5_c, complemento_de_dois_6_c, complemento_de_dois_7_c, complemento_de_dois_8_c;
  wire [7:0] complemento_de_dois_1_s, complemento_de_dois_2_s, complemento_de_dois_3_s,
       complemento_de_dois_4_s, complemento_de_dois_5_s, complemento_de_dois_6_s, complemento_de_dois_7_s,
       complemento_de_dois_8_s, multiplexer_1_out, multiplexer_2_out, multiplexer_3_out, multiplexer_4_out,
       multiplexer_5_out, multiplexer_6_out, multiplexer_7_out;

  complemento_de_dois complemento_de_dois_1 (
    .ctr(1'b1), .A({{7{1'b0}}, A[7]}), .B(N), .S(complemento_de_dois_1_s), .C(complemento_de_dois_1_c));
  Multiplexer #(.Bits(8)) multiplexer_1 (
    .sel(complemento_de_dois_1_c), .in_0(complemento_de_dois_1_s), .in_1({{7{1'b0}}, A[7]}),
    .out(multiplexer_1_out));
  complemento_de_dois complemento_de_dois_2 (
    .ctr(1'b1), .A({{6{1'b0}}, multiplexer_1_out[0], A[6]}), .B(N), .S(complemento_de_dois_2_s),
    .C(complemento_de_dois_2_c));
  Multiplexer #(.Bits(8)) multiplexer_2 (
    .sel(complemento_de_dois_2_c), .in_0(complemento_de_dois_2_s),
    .in_1({{6{1'b0}}, multiplexer_1_out[0], A[6]}), .out(multiplexer_2_out));
  complemento_de_dois complemento_de_dois_3 (
    .ctr(1'b1), .A({{5{1'b0}}, multiplexer_2_out[1:0], A[5]}), .B(N), .S(complemento_de_dois_3_s),
    .C(complemento_de_dois_3_c));
  Multiplexer #(.Bits(8)) multiplexer_3 (
    .sel(complemento_de_dois_3_c), .in_0(complemento_de_dois_3_s),
    .in_1({{5{1'b0}}, multiplexer_2_out[1:0], A[5]}), .out(multiplexer_3_out));
  complemento_de_dois complemento_de_dois_4 (
    .ctr(1'b1), .A({4'b0000, multiplexer_3_out[2:0], A[4]}), .B(N), .S(complemento_de_dois_4_s),
    .C(complemento_de_dois_4_c));
  Multiplexer #(.Bits(8)) multiplexer_4 (
    .sel(complemento_de_dois_4_c), .in_0(complemento_de_dois_4_s),
    .in_1({4'b0000, multiplexer_3_out[2:0], A[4]}), .out(multiplexer_4_out));
  complemento_de_dois complemento_de_dois_5 (
    .ctr(1'b1), .A({3'b000, multiplexer_4_out[3:0], A[3]}), .B(N), .S(complemento_de_dois_5_s),
    .C(complemento_de_dois_5_c));
  Multiplexer #(.Bits(8)) multiplexer_5 (
    .sel(complemento_de_dois_5_c), .in_0(complemento_de_dois_5_s),
    .in_1({3'b000, multiplexer_4_out[3:0], A[3]}), .out(multiplexer_5_out));
  complemento_de_dois complemento_de_dois_6 (
    .ctr(1'b1), .A({2'b00, multiplexer_5_out[4:0], A[2]}), .B(N), .S(complemento_de_dois_6_s),
    .C(complemento_de_dois_6_c));
  Multiplexer #(.Bits(8)) multiplexer_6 (
    .sel(complemento_de_dois_6_c), .in_0(complemento_de_dois_6_s),
    .in_1({2'b00, multiplexer_5_out[4:0], A[2]}), .out(multiplexer_6_out));
  complemento_de_dois complemento_de_dois_7 (
    .ctr(1'b1), .A({1'b0, multiplexer_6_out[5:0], A[1]}), .B(N), .S(complemento_de_dois_7_s),
    .C(complemento_de_dois_7_c));
  Multiplexer #(.Bits(8)) multiplexer_7 (
    .sel(complemento_de_dois_7_c), .in_0(complemento_de_dois_7_s),
    .in_1({1'b0, multiplexer_6_out[5:0], A[1]}), .out(multiplexer_7_out));
  complemento_de_dois complemento_de_dois_8 (
    .ctr(1'b1), .A({multiplexer_7_out[6:0], A[0]}), .B(N), .S(complemento_de_dois_8_s),
    .C(complemento_de_dois_8_c));
  Multiplexer #(.Bits(8)) multiplexer_8 (
    .sel(complemento_de_dois_8_c), .in_0(complemento_de_dois_8_s), .in_1({multiplexer_7_out[6:0], A[0]}),
    .out(R));
  not not_1 (Q[0], complemento_de_dois_8_c);
  not not_2 (Q[1], complemento_de_dois_7_c);
  not not_3 (Q[2], complemento_de_dois_6_c);
  not not_4 (Q[3], complemento_de_dois_5_c);
  not not_5 (Q[4], complemento_de_dois_4_c);
  not not_6 (Q[5], complemento_de_dois_3_c);
  not not_7 (Q[6], complemento_de_dois_2_c);
  not not_8 (Q[7], complemento_de_dois_1_c);
endmodule
