// Digital circuit multiplicador-completo.dig as structural Verilog
module multiplicador_completo (
  input  B8,
  input  B7,
  input  B6,
  input  B5,
  input  B4,
  input  B3,
  input  B2,
  input  B1,
  input  multiplicador1,
  output M8,
  output M7,
  output M6,
  output M5,
  output M4,
  output M3,
  output M2,
  output M1
);

  and and_1 (M8, B8, multiplicador1);
  and and_2 (M7, B7, multiplicador1);
  and and_3 (M6, B6, multiplicador1);
  and and_4 (M5, B5, multiplicador1);
  and and_5 (M4, B4, multiplicador1);
  and and_6 (M3, B3, multiplicador1);
  and and_7 (M2, B2, multiplicador1);
  and and_8 (M1, B1, multiplicador1);
endmodule
