// Digital circuit multiplicador-final-8bits.dig as structural Verilog
module multiplicador_final_8bits (
  input  [7:0] A,
  input  [7:0] N,
  output [7:0] AC,
  output [7:0] MQ
);

  wire circuito_soma_1_cout, circuito_soma_1_s2, circuito_soma_1_s3, circuito_soma_1_s4, circuito_soma_1_s5,
       circuito_soma_1_s6, circuito_soma_1_s7, circuito_soma_1_s8, circuito_soma_1_s9, circuito_soma_2_cout,
       circuito_soma_2_s2, circuito_soma_2_s3, circuito_soma_2_s4, circuito_soma_2_s5, circuito_soma_2_s6,
       circuito_soma_2_s7, circuito_soma_2_s8, circuito_soma_2_s9, circuito_soma_3_cout, circuito_soma_3_s2,
       circuito_soma_3_s3, circuito_soma_3_s4, circuito_soma_3_s5, circuito_soma_3_s6, circuito_soma_3_s7,
       circuito_soma_3_s8, circuito_soma_3_s9, circuito_soma_4_cout, circuito_soma_4_s2, circuito_soma_4_s3,
       circuito_soma_4_s4, circuito_soma_4_s5, circuito_soma_4_s6, circuito_soma_4_s7, circuito_soma_4_s8,
       circuito_soma_4_s9, circuito_soma_5_cout, circuito_soma_5_s2, circuito_soma_5_s3, circuito_soma_5_s4,
       circuito_soma_5_s5, circuito_soma_5_s6, circuito_soma_5_s7, circuito_soma_5_s8, circuito_soma_5_s9,
       circuito_soma_6_cout, circuito_soma_6_s2, circuito_soma_6_s3, circuito_soma_6_s4, circuito_soma_6_s5,
       circuito_soma_6_s6, circuito_soma_6_s7, circuito_soma_6_s8, circuito_soma_6_s9,
       multiplicador_completo_1_m1, multiplicador_completo_1_m2, multiplicador_completo_1_m3,
       multiplicador_completo_1_m4, multiplicador_completo_1_m5, multiplicador_completo_1_m6,
       multiplicador_completo_1_m7, multiplicador_completo_1_m8, multiplicador_completo_2_m1,
       multiplicador_completo_2_m2, multiplicador_completo_2_m3, multiplicador_completo_2_m4,
       multiplicador_completo_2_m5, multiplicador_completo_2_m6, multiplicador_completo_2_m7,
       multiplicador_completo_2_m8, multiplicador_completo_3_m1, multiplicador_completo_3_m2,
       multiplicador_completo_3_m3, multiplicador_completo_3_m4, multiplicador_completo_3_m5,
       multiplicador_completo_3_m6, multiplicador_completo_3_m7, multiplicador_completo_3_m8,
       multiplicador_completo_4_m1, multiplicador_completo_4_m2, multiplicador_completo_4_m3,
       multiplicador_completo_4_m4, multiplicador_completo_4_m5, multiplicador_completo_4_m6,
       multiplicador_completo_4_m7, multiplicador_completo_4_m8, multiplicador_completo_5_m1,
       multiplicador_completo_5_m2, multiplicador_completo_5_m3, multiplicador_completo_5_m4,
       multiplicador_completo_5_m5, multiplicador_completo_5_m6, multiplicador_completo_5_m7,
       multiplicador_completo_5_m8, multiplicador_completo_6_m1, multiplicador_completo_6_m2,
       multiplicador_completo_6_m3, multiplicador_completo_6_m4, multiplicador_completo_6_m5,
       multiplicador_completo_6_m6, multiplicador_completo_6_m7, multiplicador_completo_6_m8,
       multiplicador_completo_7_m1, multiplicador_completo_7_m2, multiplicador_completo_7_m3,
       multiplicador_completo_7_m4, multiplicador_completo_7_m5, multiplicador_completo_7_m6,
       multiplicador_completo_7_m7, multiplicador_completo_7_m8, multiplicador_completo_8_m1,
       multiplicador_completo_8_m2, multiplicador_completo_8_m3, multiplicador_completo_8_m4,
       multiplicador_completo_8_m5, multiplicador_completo_8_m6, multiplicador_completo_8_m7,
       multiplicador_completo_8_m8;

  multiplicador_completo multiplicador_completo_1 (
    .B8(A[7]), .B7(A[6]), .B6(A[5]), .B5(A[4]), .B4(A[3]), .B3(A[2]), .B2(A[1]), .B1(A[0]),
    .multiplicador1(N[7]), .M8(multiplicador_completo_1_m8), .M7(multiplicador_completo_1_m7),
    .M6(multiplicador_completo_1_m6), .M5(multiplicador_completo_1_m5), .M4(multiplicador_completo_1_m4),
    .M3(multiplicador_completo_1_m3), .M2(multiplicador_completo_1_m2), .M1(multiplicador_completo_1_m1));
  multiplicador_completo multiplicador_completo_2 (
    .B8(A[7]), .B7(A[6]), .B6(A[5]), .B5(A[4]), .B4(A[3]), .B3(A[2]), .B2(A[1]), .B1(A[0]),
    .multiplicador1(N[6]), .M8(multiplicador_completo_2_m8), .M7(multiplicador_completo_2_m7),
    .M6(multiplicador_completo_2_m6), .M5(multiplicador_completo_2_m5), .M4(multiplicador_completo_2_m4),
    .M3(multiplicador_completo_2_m3), .M2(multiplicador_completo_2_m2), .M1(multiplicador_completo_2_m1));
  multiplicador_completo multiplicador_completo_3 (
    .B8(A[7]), .B7(A[6]), .B6(A[5]), .B5(A[4]), .B4(A[3]), .B3(A[2]), .B2(A[1]), .B1(A[0]),
    .multiplicador1(N[5]), .M8(multiplicador_completo_3_m8), .M7(multiplicador_completo_3_m7),
    .M6(multiplicador_completo_3_m6), .M5(multiplicador_completo_3_m5), .M4(multiplicador_completo_3_m4),
    .M3(multiplicador_completo_3_m3), .M2(multiplicador_completo_3_m2), .M1(multiplicador_completo_3_m1));
  multiplicador_completo multiplicador_completo_4 (
    .B8(A[7]), .B7(A[6]), .B6(A[5]), .B5(A[4]), .B4(A[3]), .B3(A[2]), .B2(A[1]), .B1(A[0]),
    .multiplicador1(N[4]), .M8(multiplicador_completo_4_m8), .M7(multiplicador_completo_4_m7),
    .M6(multiplicador_completo_4_m6), .M5(multiplicador_completo_4_m5), .M4(multiplicador_completo_4_m4),
    .M3(multiplicador_completo_4_m3), .M2(multiplicador_completo_4_m2), .M1(multiplicador_completo_4_m1));
  multiplicador_completo multiplicador_completo_5 (
    .B8(A[7]), .B7(A[6]), .B6(A[5]), .B5(A[4]), .B4(A[3]), .B3(A[2]), .B2(A[1]), .B1(A[0]),
    .multiplicador1(N[3]), .M8(multiplicador_completo_5_m8), .M7(multiplicador_completo_5_m7),
    .M6(multiplicador_completo_5_m6), .M5(multiplicador_completo_5_m5), .M4(multiplicador_completo_5_m4),
    .M3(multiplicador_completo_5_m3), .M2(multiplicador_completo_5_m2), .M1(multiplicador_completo_5_m1));
  multiplicador_completo multiplicador_completo_6 (
    .B8(A[7]), .B7(A[6]), .B6(A[5]), .B5(A[4]), .B4(A[3]), .B3(A[2]), .B2(A[1]), .B1(A[0]),
    .multiplicador1(N[2]), .M8(multiplicador_completo_6_m8), .M7(multiplicador_completo_6_m7),
    .M6(multiplicador_completo_6_m6), .M5(multiplicador_completo_6_m5), .M4(multiplicador_completo_6_m4),
    .M3(multiplicador_completo_6_m3), .M2(multiplicador_completo_6_m2), .M1(multiplicador_completo_6_m1));
  multiplicador_completo multiplicador_completo_7 (
    .B8(A[7]), .B7(A[6]), .B6(A[5]), .B5(A[4]), .B4(A[3]), .B3(A[2]), .B2(A[1]), .B1(A[0]),
    .multiplicador1(N[1]), .M8(multiplicador_completo_7_m8), .M7(multiplicador_completo_7_m7),
    .M6(multiplicador_completo_7_m6), .M5(multiplicador_completo_7_m5), .M4(multiplicador_completo_7_m4),
    .M3(multiplicador_completo_7_m3), .M2(multiplicador_completo_7_m2), .M1(multiplicador_completo_7_m1));
  multiplicador_completo multiplicador_completo_8 (
    .B8(A[7]), .B7(A[6]), .B6(A[5]), .B5(A[4]), .B4(A[3]), .B3(A[2]), .B2(A[1]), .B1(A[0]),
    .multiplicador1(N[0]), .M8(multiplicador_completo_8_m8), .M7(multiplicador_completo_8_m7),
    .M6(multiplicador_completo_8_m6), .M5(multiplicador_completo_8_m5), .M4(multiplicador_completo_8_m4),
    .M3(multiplicador_completo_8_m3), .M2(multiplicador_completo_8_m2), .M1(multiplicador_completo_8_m1));
  circuito_soma circuito_soma_1 (
    .A(multiplicador_completo_8_m1), .B(1'b0), .C(multiplicador_completo_8_m2),
    .D(multiplicador_completo_7_m1), .E(multiplicador_completo_8_m3), .F(multiplicador_completo_7_m2),
    .G(multiplicador_completo_8_m4), .H(multiplicador_completo_7_m3), .I(multiplicador_completo_8_m5),
    .J(multiplicador_completo_7_m4), .K(multiplicador_completo_8_m6), .L(multiplicador_completo_7_m5),
    .M(multiplicador_completo_8_m7), .N(multiplicador_completo_7_m6), .O(multiplicador_completo_8_m8),
    .P(multiplicador_completo_7_m7), .Q(1'b0), .R(multiplicador_completo_7_m8), .S1(AC[0]),
    .S2(circuito_soma_1_s2), .S3(circuito_soma_1_s3), .S4(circuito_soma_1_s4), .S5(circuito_soma_1_s5),
    .S6(circuito_soma_1_s6), .S7(circuito_soma_1_s7), .S8(circuito_soma_1_s8), .S9(circuito_soma_1_s9),
    .Cout(circuito_soma_1_cout));
  circuito_soma circuito_soma_2 (
    .A(circuito_soma_1_s2), .B(1'b0), .C(circuito_soma_1_s3), .D(multiplicador_completo_6_m1),
    .E(circuito_soma_1_s4), .F(multiplicador_completo_6_m2), .G(circuito_soma_1_s5),
    .H(multiplicador_completo_6_m3), .I(circuito_soma_1_s6), .J(multiplicador_completo_6_m4),
    .K(circuito_soma_1_s7), .L(multiplicador_completo_6_m5), .M(circuito_soma_1_s8),
    .N(multiplicador_completo_6_m6), .O(circuito_soma_1_s9), .P(multiplicador_completo_6_m7),
    .Q(circuito_soma_1_cout), .R(multiplicador_completo_6_m8), .S1(AC[1]), .S2(circuito_soma_2_s2),
    .S3(circuito_soma_2_s3), .S4(circuito_soma_2_s4), .S5(circuito_soma_2_s5), .S6(circuito_soma_2_s6),
    .S7(circuito_soma_2_s7), .S8(circuito_soma_2_s8), .S9(circuito_soma_2_s9), .Cout(circuito_soma_2_cout));
  circuito_soma circuito_soma_3 (
    .A(circuito_soma_2_s2), .B(1'b0), .C(circuito_soma_2_s3), .D(multiplicador_completo_5_m1),
    .E(circuito_soma_2_s4), .F(multiplicador_completo_5_m2), .G(circuito_soma_2_s5),
    .H(multiplicador_completo_5_m3), .I(circuito_soma_2_s6), .J(multiplicador_completo_5_m4),
    .K(circuito_soma_2_s7), .L(multiplicador_completo_5_m5), .M(circuito_soma_2_s8),
    .N(multiplicador_completo_5_m6), .O(circuito_soma_2_s9), .P(multiplicador_completo_5_m7),
    .Q(circuito_soma_2_cout), .R(multiplicador_completo_5_m8), .S1(AC[2]), .S2(circuito_soma_3_s2),
    .S3(circuito_soma_3_s3), .S4(circuito_soma_3_s4), .S5(circuito_soma_3_s5), .S6(circuito_soma_3_s6),
    .S7(circuito_soma_3_s7), .S8(circuito_soma_3_s8), .S9(circuito_soma_3_s9), .Cout(circuito_soma_3_cout));
  circuito_soma circuito_soma_4 (
    .A(circuito_soma_3_s2), .B(1'b0), .C(circuito_soma_3_s3), .D(multiplicador_completo_4_m1),
    .E(circuito_soma_3_s4), .F(multiplicador_completo_4_m2), .G(circuito_soma_3_s5),
    .H(multiplicador_completo_4_m3), .I(circuito_soma_3_s6), .J(multiplicador_completo_4_m4),
    .K(circuito_soma_3_s7), .L(multiplicador_completo_4_m5), .M(circuito_soma_3_s8),
    .N(multiplicador_completo_4_m6), .O(circuito_soma_3_s9), .P(multiplicador_completo_4_m7),
    .Q(circuito_soma_3_cout), .R(multiplicador_completo_4_m8), .S1(AC[3]), .S2(circuito_soma_4_s2),
    .S3(circuito_soma_4_s3), .S4(circuito_soma_4_s4), .S5(circuito_soma_4_s5), .S6(circuito_soma_4_s6),
    .S7(circuito_soma_4_s7), .S8(circuito_soma_4_s8), .S9(circuito_soma_4_s9), .Cout(circuito_soma_4_cout));
  circuito_soma circuito_soma_5 (
    .A(circuito_soma_4_s2), .B(1'b0), .C(circuito_soma_4_s3), .D(multiplicador_completo_3_m1),
    .E(circuito_soma_4_s4), .F(multiplicador_completo_3_m2), .G(circuito_soma_4_s5),
    .H(multiplicador_completo_3_m3), .I(circuito_soma_4_s6), .J(multiplicador_completo_3_m4),
    .K(circuito_soma_4_s7), .L(multiplicador_completo_3_m5), .M(circuito_soma_4_s8),
    .N(multiplicador_completo_3_m6), .O(circuito_soma_4_s9), .P(multiplicador_completo_3_m7),
    .Q(circuito_soma_4_cout), .R(multiplicador_completo_3_m8), .S1(AC[4]), .S2(circuito_soma_5_s2),
    .S3(circuito_soma_5_s3), .S4(circuito_soma_5_s4), .S5(circuito_soma_5_s5), .S6(circuito_soma_5_s6),
    .S7(circuito_soma_5_s7), .S8(circuito_soma_5_s8), .S9(circuito_soma_5_s9), .Cout(circuito_soma_5_cout));
  circuito_soma circuito_soma_6 (
    .A(circuito_soma_5_s2), .B(1'b0), .C(circuito_soma_5_s3), .D(multiplicador_completo_2_m1),
    .E(circuito_soma_5_s4), .F(multiplicador_completo_2_m2), .G(circuito_soma_5_s5),
    .H(multiplicador_completo_2_m3), .I(circuito_soma_5_s6), .J(multiplicador_completo_2_m4),
    .K(circuito_soma_5_s7), .L(multiplicador_completo_2_m5), .M(circuito_soma_5_s8),
    .N(multiplicador_completo_2_m6), .O(circuito_soma_5_s9), .P(multiplicador_completo_2_m7),
    .Q(circuito_soma_5_cout), .R(multiplicador_completo_2_m8), .S1(AC[5]), .S2(circuito_soma_6_s2),
    .S3(circuito_soma_6_s3), .S4(circuito_soma_6_s4), .S5(circuito_soma_6_s5), .S6(circuito_soma_6_s6),
    .S7(circuito_soma_6_s7), .S8(circuito_soma_6_s8), .S9(circuito_soma_6_s9), .Cout(circuito_soma_6_cout));
  circuito_soma circuito_soma_7 (
    .A(circuito_soma_6_s2), .B(1'b0), .C(circuito_soma_6_s3), .D(multiplicador_completo_1_m1),
    .E(circuito_soma_6_s4), .F(multiplicador_completo_1_m2), .G(circuito_soma_6_s5),
    .H(multiplicador_completo_1_m3), .I(circuito_soma_6_s6), .J(multiplicador_completo_1_m4),
    .K(circuito_soma_6_s7), .L(multiplicador_completo_1_m5), .M(circuito_soma_6_s8),
    .N(multiplicador_completo_1_m6), .O(circuito_soma_6_s9), .P(multiplicador_completo_1_m7),
    .Q(circuito_soma_6_cout), .R(multiplicador_completo_1_m8), .S1(AC[6]), .S2(AC[7]), .S3(MQ[7]),
    .S4(MQ[6]), .S5(MQ[5]), .S6(MQ[4]), .S7(MQ[3]), .S8(MQ[2]), .S9(MQ[1]), .Cout(MQ[0]));

  // Other names for the same wires on the sheet: D0 = MQ[7]; D1 = MQ[6]; D2 = MQ[5]; D3 = MQ[4]; D4 = MQ[3];
  //   D5 = MQ[2]; D6 = MQ[1]; D7 = MQ[0]; M0 = AC[0]; M1 = AC[1]; M2 = AC[2]; M3 = AC[3]; M4 = AC[4]; M5 = AC[5];
  //   M6 = AC[6]; M7 = AC[7]
endmodule
